# Fritzing sketch Smart Water Quality Monitoring System 💧 (saved by Fritzing 1.0.1rc)

parts:
  LCD2004-I2C1 = LCD2004-I2C
  M1 = DOIT Esp32 DevKit v1 (30 pins long, 11 pins width) [part_number=ESP32S-PIN30]
  Water_Flow_Sensor = yf-s401 flow sensor [package=THT]
  TDS_Sensor = tds-sensor-meter-v1.0_1
  Temperature_Sensor = Humidity and Temperature Sensor DHT11
  Turbidity_Sensor = Turbidity Sensor Probe [package=THT]
  PH_Sensor = PH meter with sensor in breadboard [package=THT]
  Servo_motor = Tower Pro SG90 servo [part_number=101246]
  ZS-042_RTC1 = ZS-042 RTC Module  # not connected

nets:
  GND: LCD2004-I2C1.GND, M1.GND, PH_Sensor.pin3
  VCC: LCD2004-I2C1.VCC, M1.3V3, PH_Sensor.pin2
  N1: LCD2004-I2C1.SDA, M1.D22
  N2: LCD2004-I2C1.SCL, M1.D21
  N3: M1.D18, Temperature_Sensor.NC
  N4: M1.D19, Turbidity_Sensor.VCC
  N5: M1.D23, Water_Flow_Sensor.pin3
  N6: M1.D34, PH_Sensor.pin1
  N7: M1.D35, TDS_Sensor.pin1
  N8: M1.D13, Servo_motor.Signal
  N9: Water_Flow_Sensor.pin1, Turbidity_Sensor.pin1
  N10: Water_Flow_Sensor.pin2, Turbidity_Sensor.pin2

custom parts:
  LCD2004-I2C: A standard character display with 4x20 characters. Comes in many colors with LCM2004 IIC attached.
  DOIT Esp32 DevKit v1 (30 pins long, 11 pins width): The DOIT Esp32 DevKit v1 is one of the development board created by DOIT to evaluate the ESP-WROOM-32 module. It is based on the ESP32 microcontroller that boasts Wifi, Bluetooth, Ethernet and Low Power support all in a single chip. (vanepp) made breadboard work, adjusted pin numbering and labels and reduced size of schematic and cleaned up pcb. This chip is 30pins long (2 x15) and 11 pins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
  yf-s401 flow sensor: Flow sensors sit in line with your water line, and uses a pinwheel sensor to measure how much liquid has moved through it.
  : TDS Meter V1.0 Development Board Water Meter Filter Measuring Water Sensor Module.
  Humidity and Temperature Sensor DHT11: Digital relative humidity & temperature sensor DHT11
  Turbidity Sensor Probe: Turbidity sensor probe to the DFRobot measure module.
  PH meter with sensor in breadboard: DFrobot PH meter (SKU SEN0161)
  Tower Pro SG90 servo: Original file by John De Cristofaro http://www.adafruit.com/products/1449 Adafruit Feedback Servo (Small) Edited by: e-radionica.com 28/9/2015
